# Fritzing sketch Electronic-Kit-On-a-Shield (saved by Fritzing 0.9.3b)
circuit board: 6.88566cm x 5.36311cm
breadboards: 1

parts:
  PCB1 = Arduino Shield PCB  # not connected
  Part1 = Arduino Uno (Rev3)
  LED1 = LED - 5mm [color="Red (633nm)" package="5 mm [THT]"]
  LED2 = LED - 5mm [color="Red (633nm)" package="5 mm [THT]"]
  LED3 = LED - 5mm [color="Red (633nm)" package="5 mm [THT]"]
  LED4 = LED - 5mm [color="Red (633nm)" package="5 mm [THT]"]
  LED5 = LED - 5mm [color="Red (633nm)" package="5 mm [THT]"]
  Pot1 = Trimmer Potentiometer [maximum_resistance=10kΩ package=THT]
  Pot2 = Trimmer Potentiometer [maximum_resistance=10kΩ package=THT]
  Buzzer = Piezo Speaker
  S1 = Pushbutton [package="[THT]"]
  S2 = Pushbutton [package="[THT]"]
  Temprature = LM35 Temperature Sensor [package="TO92 [THT]"]
  Light = Photocell (LDR) [package=THT]
  IR1 = NPN-Transistor [package="TO92 [THT]"]
  Servo = Basic Servo
  Tilt = Tilt Switch [package=THT]
  R1 = Resistor [tolerance=±5% resistance=150 package="0402 [SMD]"]
  R2 = Resistor [tolerance=±5% resistance=150 package="0402 [SMD]"]
  R3 = Resistor [tolerance=±5% resistance=150 package="0402 [SMD]"]
  R4 = Resistor [tolerance=±5% resistance=150 package="0402 [SMD]"]
  R5 = Resistor [tolerance=±5% resistance=150 package="0402 [SMD]"]
  R6 = Resistor [tolerance=±5% resistance=10k package="0402 [SMD]"]
  J1 = male pin header, 2 pins [form="♂ (male)"]
  J2 = female pin header, 2 pins [form="♀ (female)"]

nets:
  N1: Part1.A0, Pot2.wiper
  N2: Part1.A1, Pot1.wiper
  N3: Part1.A2, Light.pin_0, R6.Pin_1
  N4: Part1.A3, Temprature.Vout
  N5: Part1.A4/SDA, J2.pin2
  N6: Part1.A5/SCL, J1.pin2
  N7: Part1.D8, Buzzer.pin2
  N8: Part1.D9_PWM, R5.Pin_1
  N9: Part1.D10_PWM/SS, R4.Pin_1
  N10: Part1.D11_PWM/MOSI, R3.Pin_1
  N11: Part1.D12/MISO, R2.Pin_1
  N12: Part1.D13/SCK, R1.Pin_1
  GND: Part1.GND, LED1.cathode, LED2.cathode, LED3.cathode, LED4.cathode, LED5.cathode, Pot1.leg1, Pot2.leg1, Buzzer.pin1, S1.Pin_1, S1.Pin_2, S2.Pin_1, S2.Pin_2, Temprature.GND, Light.pin_1, IR1.B, Servo.gnd, Tilt.Pin_1, J2.pin1
  N13: Part1.D2, S2.Pin_3
  N14: Part1.D3_PWM, S1.Pin_3
  N15: Part1.D5_PWM, Tilt.Pin_2
  N16: Part1.D6_PWM, Servo.pulse
  N17: Part1.D7, IR1.C
  5V: Part1.5V, Pot1.leg2, Pot2.leg2, Temprature.+Vs, IR1.E, Servo.vcc, R6.Pin_0, J1.pin1
  N18: LED1.anode, R1.Pin_0
  N19: LED2.anode, R2.Pin_0
  N20: LED3.anode, R3.Pin_0
  N21: LED4.anode, R4.Pin_0
  N22: LED5.anode, R5.Pin_0

custom parts:
  Arduino Shield PCB: Plain PCB Shaped to fit an Arduino "Shield"
